# Fritzing sketch templete of storage_room circuitory (saved by Fritzing 1.0.8)
breadboards: 2

parts:
  PV1 = Small 6V Solar Panel [mn=? mpn=? part_number=?]  # not connected
  Part1 = Arduino Mega ADK (Rev3)
  Adafruit_TFT_2_8in_Resistive_Touchshield_rev_E1 = Adafruit TFT 2.8in Resistive Touchshield rev E [mn=Adafruit mpn=#1651 part_number=#1651]
  Adafruit_bq25185_with_5V_Boost_Breakout1 = Adafruit bq25185 with 5V Boost Breakout [part_number=#6106]
  Part2 = LilyPad LiPower
  Part3 = Breadboard Power Supply Board SMD
  M1 = RioRand LM2596
  ADC1 = MCP3008 [package=dil16]
  Part4 = BME280 Breakout
  Part5 = Flora TSL2561 Lux Sensor
  Mod1 = Amica NodeMCU DEVKIT 1.0
  Part7 = Arduino Motor Shield (Rev3)
  D1 = Rectifier Diode 10A [part_number=P1000K]  # not connected
  U1 = TRANSCHIPTC5747 [package=camera_sfv24r-2st_2]
  R11 = Resistor [tolerance=±5% power=0.25W resistance=10000 package=THT]
  R12 = Resistor [tolerance=±5% power=0.25W resistance=10000 package=THT]
  R13 = Resistor [tolerance=±5% power=0.25W resistance=10000 package=THT]
  R14 = Resistor [tolerance=±5% power=0.25W resistance=10000 package=THT]
  R15 = Photocell (LDR) [power=0.25W dark_resistance_@0.01lx=300kΩ light_resistance_@100lx=400Ω luminance=10lx package=THT]
  R16 = Photocell (LDR) [power=0.25W dark_resistance_@0.01lx=300kΩ light_resistance_@100lx=400Ω luminance=10lx package=THT]
  R17 = Photocell (LDR) [power=0.25W dark_resistance_@0.01lx=300kΩ light_resistance_@100lx=400Ω luminance=10lx package=THT]
  R18 = Photocell (LDR) [power=0.25W dark_resistance_@0.01lx=300kΩ light_resistance_@100lx=400Ω luminance=10lx package=THT]
  M4 = Dagu DGServo 9g (Pan and tilt) [part_number=RS001B]
  M5 = Dagu DGServo 9g (Pan and tilt) [part_number=RS001B]

nets:
  N1: Part1.D21/SCL, Adafruit_TFT_2_8in_Resistive_Touchshield_rev_E1.SCL_3V
  N2: Part1.D20/SDA, Adafruit_TFT_2_8in_Resistive_Touchshield_rev_E1.SDA_3V, Part4.SDI/SDA, Part5.SDA
  N3: Part1.D19/RX1, M5.pulse
  N4: Part1.D18/TX1, M4.pulse
  N5: Part1.D17/RX2, Mod1.pin4
  N6: Part1.D16/TX2, Mod1.pin3
  N7: Part1.D10_PWM, ADC1.CS/SHDN
  N8: Part1.D9_PWM, U1.DOUT_6
  3V3: Part1.3V3, ADC1.VREF, ADC1.VDD
  5V: Part1.5V, Mod1.pin_30, Part7.5V
  N9: Part1.GND, Mod1.pin_29
  N10: Part1.D25, Mod1.pin_15, Part7.A1
  N11: Part1.D26, Mod1.pin_14, Part7.A2
  N12: Part1.D27, Mod1.pin_13, Part7.A3
  N13: Part1.D33, Mod1.pin_12, Part7.A4
  N14: Part1.D50/MISO, ADC1.Dout
  N15: Part1.D51/MOSI, ADC1.Din
  N16: Part1.D52/SCK, ADC1.CLK
  VIN: Adafruit_bq25185_with_5V_Boost_Breakout1.VIN, Part2.+, Part3.VCC
  GND: Adafruit_bq25185_with_5V_Boost_Breakout1.GND, Part2.GND, Part3.GND, M1.Pin_2, ADC1.DGND, Part5.GND
  N17: ADC1.CH0, R11.Pin_0, R15.pin_1
  N18: ADC1.CH1, R12.Pin_0, R16.pin_1
  N19: ADC1.CH2, R13.Pin_0, R17.pin_1
  N20: ADC1.CH3, R14.Pin_0, R18.pin_1
  N21: Part4.SCK/SCL, Part5.SCL
  N22: U1.SCLK, U1.AGND, U1.AVDD28, U1.RESET_N
  N23: U1.DOUT_0, U1.DOUT_1, U1.DOUT_2, U1.DOUT_3, U1.DOUT_4
  N24: U1.DOUT_7, U1.DOUT_8, U1.VCLK_OUT, U1.VALIDH, U1.VALIDV
  N25: U1.PS1, U1.PS2, U1.SHIELD, U1.LED_CTRL
  N26: R11.Pin_1, R12.Pin_1, R13.Pin_1, R14.Pin_1, M5.gnd
  N27: R15.pin_0, R16.pin_0, R17.pin_0, R18.pin_0, M5.vcc

notes:
  This section is for heater, humidifier, & Fan
  Not every part label in the github where present here so you would have to buy the physical ones to have your desire connection
